# Fritzing sketch Led (saved by Fritzing 0.9.4)
breadboards: 1

parts:
  Raspberry_Pi_1 = Raspberry Pi 3 [part_number=RPI-3-V1.2]
  Q1 = MOSFET-NCHANNEL [package=to220v]
  LED1 = smd LED [color="Red (633nm)" package="0805 [SMD]"]
  VCC1 = Battery

nets:
  N1: Raspberry_Pi_1.GND, Q1.S, VCC1.-
  N2: Raspberry_Pi_1.GPIO17, Q1.G
  N3: Q1.D, LED1.cathode
  N4: LED1.anode, VCC1.+
